// Logisim project exercise07_solutions.circ as structural Verilog: 1 circuit, main circuit main
module main (
  input  x0,
  input  y0,
  input  z0,
  input  x1,
  input  y1,
  input  w1,
  input  z1,
  input  x2,
  input  y2,
  input  w2,
  input  z2,
  output out_12,
  output out_13,
  output out_14
);

  wire and_1_out, and_2_out, nand_1_out, nand_2_out, nor_1_out, or_1_out, xor_1_out, xor_2_out;

  and and_1 (and_1_out, x0, y0);
  and and_2 (and_2_out, ~y0, z0);  // AND_Gate
  xor xor_1 (xor_1_out, x1, y1);
  or or_1 (or_1_out, w1, z1);
  nand nand_1 (nand_1_out, ~x2, y2);  // NAND_Gate
  nor nor_1 (nor_1_out, w2, z2);
  nor nor_2 (out_12, and_1_out, and_2_out);
  nand nand_2 (nand_2_out, xor_1_out, ~w1);  // NAND_Gate
  xor xor_2 (xor_2_out, nand_1_out, ~y2);  // XOR_Gate
  and and_3 (out_13, nand_2_out, or_1_out);
  nand nand_3 (out_14, xor_2_out, nor_1_out);
endmodule
