// Logisim project exercise11_solution.circ as structural Verilog: 1 circuit, main circuit main
module main (
  input  in_1,
  input  in_2,
  input  in_3,
  output out_4
);

  wire and_1_out, xor_1_out;

  ExactlyOne xor_1 (.out(xor_1_out), .in0(in_1), .in1(in_2), .in2(in_3));
  and and_1 (and_1_out, in_1, in_2, in_3);
  or or_1 (out_4, xor_1_out, and_1_out);
endmodule
