// Logisim project exercise12_solution.circ as structural Verilog: 1 circuit, main circuit main
module main (
  input  in_1,
  input  in_2,
  input  in_3,
  input  in_4,
  input  in_5,
  output out_6,
  output out_7,
  output out_8
);

  wire nand_2_out, nand_4_out, not_1_out, not_2_out, or_1_out, or_2_out, or_3_out, or_4_out;

  not not_1 (not_1_out, in_1);
  not not_2 (not_2_out, in_3);
  or or_1 (or_1_out, not_1_out, in_2);
  or or_2 (or_2_out, in_2, in_1);
  or or_3 (or_3_out, not_2_out, in_5);
  or or_4 (or_4_out, in_5, in_3);
  nand nand_1 (out_6, or_1_out, nand_2_out);
  nand nand_2 (nand_2_out, out_6, or_2_out);
  nand nand_3 (out_8, or_3_out, nand_4_out);
  nand nand_4 (nand_4_out, out_8, or_4_out);
  Multiplexer multiplexer_1 (.in0(out_6), .in1(out_8), .out(out_7), .sel(in_4));
endmodule
